// Logisim project ALU.circ as structural Verilog: 2 circuits, main circuit Multiplication
module Multiplication (
  input  [31:0] A,
  input  [31:0] B,
  output [31:0] Low,
  output [31:0] High
);

  wire carry_low, NegOut, selectorA, selectorB;
  wire [31:0] adder_1_out, adder_2_out, multiplexer_1_out, multiplexer_2_out, multiplier_1_cout,
       multiplier_1_out, not_1_out, not_2_out, not_3_out, not_4_out;

  // Probe on A
  // Probe on B
  Comparator #(.width(1), .mode("unsigned")) comparator_1 (.a(1'b1), .b(A[31]), .eq(selectorA));  // open: gt, lt
  assign not_1_out = ~A;  // NOT_Gate not_1, 32 bits wide
  assign not_2_out = ~B;  // NOT_Gate not_2, 32 bits wide
  Comparator #(.width(1)) comparator_2 (.a(B[31]), .b(1'b1), .eq(selectorB));  // open: gt, lt
  Multiplexer #(.width(32), .enable("false")) multiplexer_1 (
    .in0(A), .in1(not_1_out), .out(multiplexer_1_out), .sel(selectorA));
  Multiplexer #(.width(32), .enable("false")) multiplexer_2 (
    .in0(B), .in1(not_2_out), .out(multiplexer_2_out), .sel(selectorB));
  Multiplier #(.width(32)) multiplier_1 (
    .a(multiplexer_1_out), .b(multiplexer_2_out), .out(multiplier_1_out), .cout(multiplier_1_cout));  // open: cin
  xor xor_1 (NegOut, selectorA, selectorB);
  assign not_3_out = ~multiplier_1_out;  // NOT_Gate not_3, 32 bits wide
  assign not_4_out = ~multiplier_1_cout;  // NOT_Gate not_4, 32 bits wide
  Adder #(.width(32)) adder_1 (.a(not_3_out), .b(32'h1), .out(adder_1_out), .cout(carry_low));  // open: cin
  Adder #(.width(32)) adder_2 (.a(not_4_out), .b({32{1'b0}}), .out(adder_2_out), .cin(carry_low));  // open: cout
  // Probe on Low
  Multiplexer #(.width(32), .enable("false")) multiplexer_3 (
    .in0(multiplier_1_out), .in1(adder_1_out), .out(Low), .sel(NegOut));
  Multiplexer #(.width(32), .enable("false")) multiplexer_4 (
    .in0(multiplier_1_cout), .in1(adder_2_out), .out(High), .sel(NegOut));
  // Probe on High
endmodule

module Division (
  input  [31:0] A,
  input  [31:0] B,
  output [31:0] Low,
  output [31:0] High
);

  wire is_zero;
  wire [1:0] selector;
  wire [31:0] cte, minus_neg_division, minus_positive_division, multiplexer_1_out, multiplexer_2_out,
       multiplication_1_low, neg_division, not_3_out, not_4_out, positive_division, rest;

  // Probe on A
  // Probe on B
  assign minus_positive_division = ~positive_division;  // NOT_Gate not_1, 32 bits wide
  Adder #(.width(32)) adder_1 (.a(positive_division), .b(cte), .out(neg_division));  // open: cin, cout
  assign minus_neg_division = ~neg_division;  // NOT_Gate not_2, 32 bits wide
  Comparator #(.width(1), .mode("unsigned")) comparator_1 (.a(1'b1), .b(A[31]), .eq(selector[1]));  // open: gt, lt
  assign not_3_out = ~A;  // NOT_Gate not_3, 32 bits wide
  assign not_4_out = ~B;  // NOT_Gate not_4, 32 bits wide
  Comparator #(.width(1)) comparator_2 (.a(B[31]), .b(1'b1), .eq(selector[0]));  // open: gt, lt
  Comparator #(.width(32)) comparator_3 (.a(rest), .b({32{1'b0}}), .eq(is_zero));  // open: gt, lt
  Multiplexer #(.width(32), .enable("false")) multiplexer_1 (
    .in0(A), .in1(not_3_out), .out(multiplexer_1_out), .sel(selector[1]));
  Multiplexer #(.width(32), .enable("false")) multiplexer_2 (
    .in0(B), .in1(not_4_out), .out(multiplexer_2_out), .sel(selector[0]));
  Divider #(.width(32)) divider_1 (
    .a(multiplexer_1_out), .b(multiplexer_2_out), .out(positive_division), .rem(rest));  // open: upper
  Multiplexer #(.width(32), .enable("false")) multiplexer_3 (.in0(32'h1), .in1({32{1'b0}}), .out(cte), .sel(is_zero));
  Multiplication multiplication_1 (.A(B), .B(Low), .Low(multiplication_1_low));  // open: High
  Multiplexer #(.select(2), .width(32), .enable("false")) multiplexer_4 (
    .in0(positive_division), .in1(minus_positive_division), .in2(minus_neg_division), .in3(neg_division),
    .out(Low), .sel(selector));
  Subtractor #(.width(32)) subtractor_1 (.a(A), .b(multiplication_1_low), .out(High));  // open: bin, bout
  // Probe on High
  // Probe on Low

  // Other names for the same wires on the sheet: result[31:0] = Low; selectorB = selector[0]; selectorA = selector[1]
endmodule
